# Fritzing sketch power-rtc (saved by Fritzing 0.9.4)
breadboards: 1

parts:
  ATMEGA = Arduino Pro Mini v13
  Pi_Zero = Raspberry Pi Zero
  R1 = Resistor [tolerance=±5% resistance=330 package=THT]
  ZS-042_RTC1 = ZS-042 RTC Module
  RUN_RESET_PI = male pin header, 1 pin [form="♂ (male)"]
  LED1 = LED - 3mm [color="Red (633nm)" package="3 mm [THT]"]

nets:
  GND: ATMEGA.GND, Pi_Zero.pin_9, Pi_Zero.pin_39, R1.Pin_0, ZS-042_RTC1.GND
  VCC: ATMEGA.VCC, Pi_Zero.pin_1, ZS-042_RTC1.VCC
  N1: ATMEGA.D9_PWM, LED1.anode
  N2: ATMEGA.D8, Pi_Zero.pin_13
  N3: ATMEGA.D4, RUN_RESET_PI.pin1
  N4: ATMEGA.D3_PWM, Pi_Zero.pin_7
  N5: ATMEGA.D2, Pi_Zero.pin_11
  N6: Pi_Zero.pin_3, ZS-042_RTC1.SDA
  N7: Pi_Zero.pin_5, ZS-042_RTC1.SCL
  N8: R1.Pin_1, LED1.cathode
